// Logisim project traffic_light_simulator.circ as structural Verilog: 1 circuit, main circuit main
module main (
);

  wire clock_1_out;
  wire [9:0] counter_1_q;
  wire [11:0] rom_1_data;

  Clock clock_1 (.out(clock_1_out));
  Counter #(.width(10), .max('h3ff)) counter_1 (
    .Q(counter_1_q), .clk(clock_1_out));  // open: load, D, count, carry, clr
  ROM #(.addrWidth(10), .dataWidth(12)) rom_1 (.addr(counter_1_q), .data(rom_1_data), .sel(1'b1));
  LED led_1 (.in(rom_1_data[2]));
  LED led_2 (.in(rom_1_data[0]));
  LED led_3 (.in(rom_1_data[3]));
  LED led_4 (.in(rom_1_data[1]));
  LED led_5 (.in(rom_1_data[4]));
  _7_Segment_Display u_7_segment_display_1 (
    .g(rom_1_data[11]), .f(rom_1_data[10]), .a(rom_1_data[5]), .b(rom_1_data[6]), .e(rom_1_data[9]),
    .d(rom_1_data[8]), .c(rom_1_data[7]));  // open: dp

  // Notes on the sheet:
  //   contents of rom_1 (hex, n*v repeats v):
  //   005 005 005 005 005 005 005 005          005 005 005 005 005 005 005 006          006 006 006 006
  //   006 006 006 006          006 006 006 006 006 006 006 006          006 006 006 006 006 006 006 006
  //   006 006 006 006 006 006 006 006          006 006 006 006 006 006 006 006          006 006 006 006
  //   006 006 006 006          006 006 006 006 006 006 006 005          005 005 005 005 005 005 005 005
  //   005 005 005 005 005 005 005 00D          00D 00D 00D 00D 00D 00D 00D DF1          DF1 DF1 DF1 DF1
  //   DF1 DF1 DF1 FF1          FF1 FF1 FF1 FF1 FF1 FF1 FF1 0F1          0F1 0F1 0F1 0F1 0F1 0F1 0F1 FB1
  //   FB1 FB1 FB1 FB1 FB1 FB1 FB1 DB1          DB1 DB1 DB1 DB1 DB1 DB1 DB1 CD1          CD1 CD1 CD1 CD1
  //   CD1 CD1 CD1 9F1          9F1 9F1 9F1 9F1 9F1 9F1 9F1 B71          B71 B71 B71 B71 B71 B71 B71 0D1
  //   0D1 0D1 0D1 0D1 0D1 0D1 0D1 009          009 009 009 009 009 009 009 005          005 005 005 005
  //   005 005 005 005          005 005 005 005 005 005 005 006          006 006 006 006 006 006 006 006
  //   006 006 006 006 006 006 006 006          006 006 006 006 006 006 006 006          006 006 006 006
  //   006 006 006 006          006 006 006 006 006 006 006 006
endmodule
